# Fritzing sketch wiring (saved by Fritzing 0.9.3b)

parts:
  Raspberry_Pi2/3 = Raspberry Pi 2
  R11 = Resistor [tolerance=±5% resistance=330 package=THT]
  R7 = Resistor [tolerance=±5% resistance=330 package=THT]
  R8 = Resistor [tolerance=±5% resistance=330 package=THT]
  R9 = Resistor [tolerance=±5% resistance=330 package=THT]
  R10 = Resistor [tolerance=±5% resistance=330 package=THT]
  R1 = Resistor [tolerance=±5% resistance=330 package=THT]
  R2 = Resistor [tolerance=±5% resistance=330 package=THT]
  R3 = Resistor [tolerance=±5% resistance=330 package=THT]
  R4 = Resistor [tolerance=±5% resistance=330 package=THT]
  R6 = Resistor [tolerance=±5% resistance=330 package=THT]
  R5 = Resistor [tolerance=±5% resistance=330 package=THT]
  X2 = DB9 Connector [package=db9]
  X1 = DB9 Connector [package=db9]

nets:
  N1: Raspberry_Pi2/3.ID_SD, R1.Pin_0
  N2: Raspberry_Pi2/3.GIPO5, R2.Pin_0
  N3: Raspberry_Pi2/3.GIPO6, R3.Pin_0
  N4: Raspberry_Pi2/3.GIPO13, R4.Pin_0
  N5: Raspberry_Pi2/3.GIPO19, R5.Pin_1
  N6: Raspberry_Pi2/3.GIPO26, R6.Pin_1
  N7: Raspberry_Pi2/3.GND, X2.8, X1.8
  N8: Raspberry_Pi2/3.GIPO16, R11.Pin_1
  N9: Raspberry_Pi2/3.ID_SC, R10.Pin_0
  N10: Raspberry_Pi2/3.GIPO7, R9.Pin_0
  N11: Raspberry_Pi2/3.GIPO8, R8.Pin_0
  N12: Raspberry_Pi2/3.GIPO25, R7.Pin_0
  N13: R11.Pin_0, X2.6
  N14: R7.Pin_1, X2.1
  N15: R8.Pin_1, X2.2
  N16: R9.Pin_1, X2.3
  N17: R10.Pin_1, X2.4
  N18: R1.Pin_1, X1.1
  N19: R2.Pin_1, X1.2
  N20: R3.Pin_1, X1.3
  N21: R4.Pin_1, X1.4
  N22: R6.Pin_0, X1.9
  N23: R5.Pin_0, X1.6

custom parts:
  DB9 Connector: DB9 Connector Standard DB9 (D-Sub 9) serial connector. Can be used for CAN bus as well as RS485 and RS232. Footprint production proven. Spark Fun Electronics SKU : PRT-00429
